// Logisim project 225_lab1.circ as structural Verilog: 3 circuits, main circuit main
module main (
  input  A,
  input  B,
  input  Cin,
  input  A_2,
  input  B_2,
  input  Cin_2,
  input  A1,
  input  B1,
  input  A2,
  input  B2,
  input  A3,
  input  B3,
  input  A4,
  input  B4,
  output S,
  output Cout,
  output S_2,
  output Cout_2,
  output S1,
  output S2,
  output S3,
  output S4,
  output Cout_3
);

  wire Full_Adder_2_cout, Full_Adder_3_cout, Full_Adder_cout, Half_Adder_2_cout, Half_Adder_cout,
       Half_Adder_s1;

  HalfAdder Half_Adder (.A(A_2), .B(B_2), .S1(Half_Adder_s1), .Cout(Half_Adder_cout));
  xor xor_1 (S, A, B);
  and and_1 (Cout, A, B);
  HalfAdder Half_Adder_2 (.A(Cin), .B(Half_Adder_s1), .S1(S_2), .Cout(Half_Adder_2_cout));
  FullAdder Full_Adder (.Cin(Cin_2), .A(A1), .B(B1), .S(S1), .Cout(Full_Adder_cout));
  FullAdder Full_Adder_2 (.Cin(Full_Adder_cout), .A(A2), .B(B2), .S(S2), .Cout(Full_Adder_2_cout));
  or or_1 (Cout_2, Half_Adder_2_cout, Half_Adder_cout);
  FullAdder Full_Adder_3 (.Cin(Full_Adder_2_cout), .A(A3), .B(B3), .S(S3), .Cout(Full_Adder_3_cout));
  FullAdder Full_Adder_4 (.Cin(Full_Adder_3_cout), .A(A4), .B(B4), .S(S4), .Cout(Cout_3));
endmodule

module HalfAdder (
  input  A,
  input  B,
  output S1,
  output Cout
);

  xor xor_1 (S1, A, B);
  and and_1 (Cout, A, B);
endmodule

module FullAdder (
  input  Cin,
  input  A,
  input  B,
  output S,
  output Cout
);

  wire halfadder_1_cout, halfadder_1_s1, halfadder_2_cout;

  HalfAdder halfadder_1 (.A(A), .B(B), .S1(halfadder_1_s1), .Cout(halfadder_1_cout));
  HalfAdder halfadder_2 (.A(Cin), .B(halfadder_1_s1), .S1(S), .Cout(halfadder_2_cout));
  or or_1 (Cout, halfadder_2_cout, halfadder_1_cout);
endmodule
