// Logisim project 225_lab2.circ as structural Verilog: 1 circuit, main circuit main
module main (
  input  a,
  input  b,
  input  c,
  output cout
);

  wire g1_out, g2_out, g3_out;

  and g1 (g1_out, a, b);
  and g2 (g2_out, a, c);
  and g3 (g3_out, b, c);
  or g4 (cout, g1_out, g2_out, g3_out);
endmodule
